# Fritzing sketch bike (saved by Fritzing 0.9.1b)
breadboards: 1

parts:
  reed_switch = SWITCH-MOMENTARY-2 [package=tactile-switch-1101ne]
  velocimetro = RJ45 Jack [package=rj45-8]
  guidon = RJ45 Jack [package=rj45-8]
  encoder_+_switch = IC, SIP package, 5 pins [chip_label=IC]
  para_arduino = RJ45 Jack [package=rj45-8]
  velocimetro_ou_guidon = RJ45 Jack [package=rj45-8]
  velocimetro_ou_guidon_2 = RJ45 Jack [package=rj45-8]

nets:
  N1: reed_switch.1, velocimetro.2
  N2: reed_switch.2, velocimetro.3
  N3: guidon.1, encoder_+_switch.pin1
  N4: guidon.2, encoder_+_switch.pin2
  N5: guidon.4, encoder_+_switch.pin4
  N6: guidon.5, encoder_+_switch.pin5
  N7: guidon.6, encoder_+_switch.pin3
  N8: para_arduino.1, velocimetro_ou_guidon.1, velocimetro_ou_guidon_2.1
  N9: para_arduino.2, para_arduino.8, velocimetro_ou_guidon.2, velocimetro_ou_guidon_2.2
  N10: para_arduino.3, velocimetro_ou_guidon.3, velocimetro_ou_guidon_2.3
  N11: para_arduino.4, velocimetro_ou_guidon.4, velocimetro_ou_guidon_2.4
  N12: para_arduino.5, velocimetro_ou_guidon.5, velocimetro_ou_guidon_2.5
  N13: para_arduino.6, velocimetro_ou_guidon.6, velocimetro_ou_guidon_2.6
  N14: para_arduino.7, velocimetro_ou_guidon.7, velocimetro_ou_guidon_2.7

notes:
  o fio azul eh o status (gnd + pin8)
