# Fritzing sketch box (saved by Fritzing 0.9.1b)
breadboards: 1

parts:
  arduino_mega = Arduino Mega ADK (Rev3)
  bike_1 = RJ45 Jack [package=rj45-8]
  bike_2 = RJ45 Jack [package=rj45-8]
  bike_3 = RJ45 Jack [package=rj45-8]
  bike_4 = RJ45 Jack [package=rj45-8]

nets:
  N1: arduino_mega.D21/SCL, bike_4.4
  N2: arduino_mega.D20/SDA, bike_4.3
  N3: arduino_mega.D19/RX1, bike_3.8
  N4: arduino_mega.D18/TX1, bike_3.7
  N5: arduino_mega.D17/RX2, bike_3.6
  N6: arduino_mega.D16/TX2, bike_3.5
  N7: arduino_mega.D15/RX3, bike_3.4
  N8: arduino_mega.D14/TX3, bike_3.3
  N9: arduino_mega.GND, bike_1.2, bike_2.2, bike_3.2, bike_4.2
  N10: arduino_mega.D13_PWM, bike_2.8
  N11: arduino_mega.D12_PWM, bike_2.7
  N12: arduino_mega.D11_PWM, bike_2.6
  N13: arduino_mega.D10_PWM, bike_2.5
  N14: arduino_mega.D9_PWM, bike_2.4
  N15: arduino_mega.D8_PWM, bike_2.3
  N16: arduino_mega.IOREF, arduino_mega.5V, bike_1.1, bike_2.1, bike_3.1, bike_4.1
  N17: arduino_mega.D2_PWM, bike_1.3
  N18: arduino_mega.D3_PWM, bike_1.4
  N19: arduino_mega.D4_PWM, bike_1.5
  N20: arduino_mega.D5_PWM, bike_1.6
  N21: arduino_mega.D6_PWM, bike_1.7
  N22: arduino_mega.D7_PWM, bike_1.8
  N23: arduino_mega.D22, bike_4.5
  N24: arduino_mega.D23, bike_4.6
  N25: arduino_mega.D24, bike_4.7
  N26: arduino_mega.D25, bike_4.8

notes:
  atenção na ordem dos pinos!
